# Fritzing sketch Cat Toy (saved by Fritzing 0.9.2b)
circuit board: 8.46667cm x 5.64444cm
breadboards: 1

parts:
  J1 = Basic Servo
  USB = FTDI Basic Programmer
  U1 = Voltage Regulator - 3.3V [package="TO220 [THT]"]
  U2 = ESP8266 WiFi Module [part_number=ESP8266]

nets:
  GND: J1.gnd, USB.GND, U1.GND, U2.GND
  N1: J1.vcc, USB.POWER, U1.input_voltage
  N2: J1.pulse, U2.GPIO_0
  N3: USB.RXI, U2.TXD
  N4: USB.TXO, U2.RXD
  N5: U1.output_voltage, U2.VCC

custom parts:
  ESP8266 WiFi Module: Generic WiFi Module based on the ESP8266 with onboard PCB antenna and UART communications
